// Logisim project FullAdder.circ as structural Verilog: 2 circuits, main circuit main
module main (
  input  A,
  input  B,
  input  Cin,
  output Suma,
  output Cout
);

  wire and_1_out, and_2_out, xor_1_out;

  xor xor_1 (xor_1_out, A, B);
  and and_1 (and_1_out, xor_1_out, Cin);
  and and_2 (and_2_out, A, B);
  xor xor_2 (Suma, xor_1_out, Cin);
  or or_1 (Cout, and_1_out, and_2_out);
endmodule

module AdderSubtractor8 (
  input  T,
  input  [7:0] in_2,
  input  [7:0] in_3,
  output Co,
  output out_5,
  output out_6,
  output out_7,
  output out_8,
  output out_9,
  output out_10,
  output out_11,
  output out_12,
  output OF
);

  wire main_2_cout, main_3_cout, main_4_cout, main_5_cout, main_6_cout, main_7_cout, main_8_cout, xor_2_out,
       xor_3_out, xor_4_out, xor_5_out, xor_6_out, xor_7_out, xor_8_out, xor_9_out;

  xor xor_1 (OF, Co, main_2_cout);
  xor xor_2 (xor_2_out, in_3[7], T);
  main main_1 (.A(in_2[7]), .B(xor_2_out), .Cin(main_2_cout), .Suma(out_5), .Cout(Co));
  xor xor_3 (xor_3_out, in_3[6], T);
  main main_2 (.A(in_2[6]), .B(xor_3_out), .Cin(main_3_cout), .Suma(out_6), .Cout(main_2_cout));
  xor xor_4 (xor_4_out, in_3[5], T);
  main main_3 (.A(in_2[5]), .B(xor_4_out), .Cin(main_4_cout), .Suma(out_7), .Cout(main_3_cout));
  xor xor_5 (xor_5_out, in_3[4], T);
  main main_4 (.A(in_2[4]), .B(xor_5_out), .Cin(main_5_cout), .Suma(out_8), .Cout(main_4_cout));
  xor xor_6 (xor_6_out, in_3[3], T);
  main main_5 (.A(in_2[3]), .B(xor_6_out), .Cin(main_6_cout), .Suma(out_9), .Cout(main_5_cout));
  xor xor_7 (xor_7_out, in_3[2], T);
  main main_6 (.A(in_2[2]), .B(xor_7_out), .Cin(main_7_cout), .Suma(out_10), .Cout(main_6_cout));
  xor xor_8 (xor_8_out, in_3[1], T);
  main main_7 (.A(in_2[1]), .B(xor_8_out), .Cin(main_8_cout), .Suma(out_11), .Cout(main_7_cout));
  xor xor_9 (xor_9_out, in_3[0], T);
  main main_8 (.A(in_2[0]), .B(xor_9_out), .Cin(T), .Suma(out_12), .Cout(main_8_cout));

  // Other names for the same wires on the sheet: A0 = in_2[0]; A1 = in_2[1]; A2 = in_2[2]; A3 = in_2[3]; A4 = in_2[4];
  //   A5 = in_2[5]; A6 = in_2[6]; A7 = in_2[7]; B0 = in_3[0]; B1 = in_3[1]; B2 = in_3[2]; B3 = in_3[3]; B4 = in_3[4];
  //   B5 = in_3[5]; B6 = in_3[6]; B7 = in_3[7]

  // Notes on the sheet:
  //   A
  //   B
  //   Los FAS, tambien son hechos por mi, anexo el archivo
  //   s7
  //   s6
  //   s5
  //   s4
  //   s3
  //   s2
  //   s1
  //   s0
endmodule
